// Logisim project System-funkcjonalnie-pełny-NAND-i-NOR.circ as structural Verilog: 1 circuit, main circuit main
module main (
  input  in_1,
  input  in_2,
  input  in_3,
  input  in_4,
  output out_5,
  output out_6,
  output out_7,
  output out_8,
  output out_9,
  output out_10,
  output out_11,
  output out_12,
  output out_13
);

  wire clock_1_out, nand_1_out, nand_2_out, nand_5_out, nor_1_out, nor_4_out, nor_5_out;

  Clock clock_1 (.out(clock_1_out));
  or or_1 (out_11, in_3, in_4);
  nand nand_1 (nand_1_out, in_3, in_3);
  nand nand_2 (nand_2_out, in_4, in_4);
  nor nor_1 (nor_1_out, in_3, in_4);
  not not_1 (out_5, clock_1_out);
  nand nand_3 (out_7, clock_1_out, clock_1_out);
  nor nor_2 (out_9, clock_1_out, clock_1_out);
  nand nand_4 (out_12, nand_1_out, nand_2_out);
  nor nor_3 (out_13, nor_1_out, nor_1_out);
  and and_1 (out_6, in_1, in_2);
  nor nor_4 (nor_4_out, in_1, in_1);
  nor nor_5 (nor_5_out, in_2, in_2);
  nand nand_5 (nand_5_out, in_1, in_2);
  nor nor_6 (out_8, nor_4_out, nor_5_out);
  nand nand_6 (out_10, nand_5_out, nand_5_out);

  // Notes on the sheet:
  //   OR
  //   NOT
  //   AND
endmodule
